# Fritzing sketch LDR_5V (saved by Fritzing 0.9.3b)
breadboards: 1

parts:
  Arduino = Arduino Uno (Rev3)
  R1 = Resistor [tolerance=±5% resistance=5.1k package=THT]
  R2 = Photocell (LDR) [package=THT]

nets:
  N1: Arduino.A2, R1.Pin_1, R2.pin_1
  N2: Arduino.GND, R1.Pin_0
  N3: Arduino.5V, R2.pin_0
