# Fritzing sketch single_led_pi (saved by Fritzing 0.9.3b)
breadboards: 1

parts:
  R1 = Resistor [tolerance=±5% resistance=680 package=THT]
  LED1 = LED - 3mm [color="Yellow (595nm)" package="3 mm [THT]"]
  Raspberry_Pi_1 = Raspberry Pi 3 [part_number=RPI-3-V1.2]
  Part1 = Adafruit Pi Cobbler Plus [part_number="Adafruit #2029"]

nets:
  GND: R1.Pin_0, Raspberry_Pi_1.GND, Part1.GND
  N1: R1.Pin_1, LED1.cathode
  N2: LED1.anode, Raspberry_Pi_1.GPIO19, Part1.GPIO19

notes:
  V(led)
  V(res)

custom parts:
  Adafruit Pi Cobbler Plus: The Raspberry Pi B+/Pi 2/ Pi 3 has landed on the Maker World like a 40-GPIO pinned, quad-USB ported, credit card sized bomb of DIY joy. And while you can use most of our great Model B accessories by hooking up our downgrade cable, its probably a good time to upgrade your set up and accessorize using all of the Model B+'s / Pi 2's / Pi 3's 40 pins. That's why we now carry the Adafruit Assembled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
